# Fritzing sketch Sensor inductivo 24v (saved by Fritzing 0.9.0b)
circuit board: 8.46667cm x 5.64444cm
breadboards: 1

parts:
  J1 = screw terminal, 3 pins
  J2 = male pin header, 2 pins [form="♂ (male)"]
  U1 = POT [package=pot_mammoth]
  R1 = Resistor [tolerance=±5% resistance=220 package=THT]
  J3 = screw terminal, 2 pins

nets:
  N1: J1.pin1, U1.E, R1.Pin_1, J3.pin1
  N2: J1.pin2, J2.pin1, U1.S, J3.pin2
  N3: J1.pin3, J2.pin2, U1.A, R1.Pin_0

notes:
  +
  -
  Signal
  Dpin
  GND
